# Fritzing sketch 7-Segment (saved by Fritzing 0.9.6b)
breadboards: 1

parts:
  Motor_Driver = L9110 H-bridge module [part_number="L9110 H-bridge"]
  Uno = Arduino Uno (Rev3)
  A1 = Rotary Actuator
  Motor_Driver1 = L9110 H-bridge module [part_number="L9110 H-bridge"]
  Motor_Driver2 = L9110 H-bridge module [part_number="L9110 H-bridge"]
  Motor_Driver3 = L9110 H-bridge module [part_number="L9110 H-bridge"]
  A2 = Rotary Actuator
  A3 = Rotary Actuator
  A4 = Rotary Actuator
  A5 = Rotary Actuator
  A6 = Rotary Actuator
  A7 = Rotary Actuator

nets:
  GND: Motor_Driver.GND, Uno.GND, Motor_Driver1.GND, Motor_Driver2.GND, Motor_Driver3.GND
  VCC: Motor_Driver.VCC, Motor_Driver1.VCC, Motor_Driver2.VCC, Motor_Driver3.VCC
  N1: Motor_Driver.A-IA, Uno.D13/SCK
  N2: Motor_Driver.A-IB, Uno.D12/MISO
  N3: Motor_Driver.MOTOR_A-A, A7.pin_1
  N4: Motor_Driver.MOTOR_A-B, A7.pin_2
  N5: Uno.D8, Motor_Driver1.A-IB
  N6: Uno.D9_PWM, Motor_Driver1.A-IA
  N7: Uno.D10_PWM/SS, Motor_Driver1.B-IB
  N8: Uno.D11_PWM/MOSI, Motor_Driver1.B-IA
  N9: Uno.D0/RX, Motor_Driver3.A-IB
  N10: Uno.D1/TX, Motor_Driver3.A-IA
  N11: Uno.D2, Motor_Driver3.B-IB
  N12: Uno.D3_PWM, Motor_Driver3.B-IA
  N13: Uno.D4, Motor_Driver2.A-IB
  N14: Uno.D5_PWM, Motor_Driver2.A-IA
  N15: Uno.D6_PWM, Motor_Driver2.B-IB
  N16: Uno.D7, Motor_Driver2.B-IA
  N17: A1.pin_1, Motor_Driver3.MOTOR_A-A
  N18: A1.pin_2, Motor_Driver3.MOTOR_A-B
  N19: Motor_Driver1.MOTOR_A-A, A5.pin_1
  N20: Motor_Driver1.MOTOR_A-B, A5.pin_2
  N21: Motor_Driver1.MOTOR_B-A, A6.pin_1
  N22: Motor_Driver1.MOTOR_B-B, A6.pin_2
  N23: Motor_Driver2.MOTOR_A-A, A3.pin_1
  N24: Motor_Driver2.MOTOR_A-B, A3.pin_2
  N25: Motor_Driver2.MOTOR_B-A, A4.pin_1
  N26: Motor_Driver2.MOTOR_B-B, A4.pin_2
  N27: Motor_Driver3.MOTOR_B-A, A2.pin_1
  N28: Motor_Driver3.MOTOR_B-B, A2.pin_2

custom parts:
  Rotary Actuator: Rotary Actuator using Clock Actuator
